// Logisim project m1_37069.circ as structural Verilog: 6 circuits, main circuit main
module main (
  input  x,
  input  y,
  output xANDy
);

  wire not_nor_1_xnot, transistor_1_out;

  Transistor transistor_1 (.in(1'b1), .out(transistor_1_out), .gate(x));
  NOT_NOR not_nor_1 (.x(y), .xNOT(not_nor_1_xnot));
  Transistor transistor_2 (.in(transistor_1_out), .out(xANDy), .gate(not_nor_1_xnot));
  Pull_Resistor pull_resistor_1 (.node(xANDy));
endmodule

module NOT_NOR (
  input  x,
  output xNOT
);

  Pull_Resistor pull_resistor_1 (.node(xNOT));
  Transistor transistor_1 (.in(1'b1), .out(xNOT), .gate(x));
endmodule

module NOR_T (
  input  x,
  input  y,
  output xNORy
);

  wire transistor_1_out;

  Transistor transistor_1 (.in(1'b1), .out(transistor_1_out), .gate(x));
  Pull_Resistor pull_resistor_1 (.node(xNORy));
  Transistor transistor_2 (.in(transistor_1_out), .out(xNORy), .gate(y));
endmodule

module AND_NOR (
  input  x,
  input  y,
  output xANDy
);

  wire not_nor_1_xnot, not_nor_2_xnot, transistor_1_out;

  NOT_NOR not_nor_1 (.x(x), .xNOT(not_nor_1_xnot));
  Transistor transistor_1 (.in(1'b1), .out(transistor_1_out), .gate(not_nor_1_xnot));
  NOT_NOR not_nor_2 (.x(y), .xNOT(not_nor_2_xnot));
  Transistor transistor_2 (.in(transistor_1_out), .out(xANDy), .gate(not_nor_2_xnot));
  Pull_Resistor pull_resistor_1 (.node(xANDy));
endmodule

module OR_NOR (
  input  x,
  input  y,
  output xNORy
);

  wire pull_resistor_1_node, transistor_1_out;

  Transistor transistor_1 (.in(1'b1), .out(transistor_1_out), .gate(x));
  Pull_Resistor pull_resistor_1 (.node(pull_resistor_1_node));
  Transistor transistor_2 (.in(transistor_1_out), .out(pull_resistor_1_node), .gate(y));
  NOT_NOR not_nor_1 (.x(pull_resistor_1_node), .xNOT(xNORy));
endmodule

module XOR_SOP (
  input  x,
  input  y,
  output out_3
);

  wire not_nor_1_xnot, not_nor_2_xnot, pull_resistor_1_node, transistor_1_out, transistor_2_out,
       transistor_3_out;

  Transistor transistor_1 (.in(1'b1), .out(transistor_1_out), .gate(x));
  NOT_NOR not_nor_1 (.x(x), .xNOT(not_nor_1_xnot));
  Transistor transistor_2 (.in(1'b1), .out(transistor_2_out), .gate(not_nor_1_xnot));
  NOT_NOR not_nor_2 (.x(y), .xNOT(not_nor_2_xnot));
  Transistor transistor_3 (.in(transistor_2_out), .out(transistor_3_out), .gate(y));
  Pull_Resistor pull_resistor_1 (.node(pull_resistor_1_node));
  Transistor transistor_4 (.in(transistor_1_out), .out(pull_resistor_1_node), .gate(not_nor_2_xnot));
  Pull_Resistor pull_resistor_2 (.node(transistor_3_out));
  OR_NOR or_nor_1 (.x(pull_resistor_1_node), .y(transistor_3_out), .xNORy(out_3));
endmodule
